// Logisim project NANO_3-bit_Parity.circ as structural Verilog: 7 circuits, main circuit 3-Input Odd Parity
module main (
  output out_1
);

  wire dip_7404_1_p2, dip_7404_1_p4, dip_7404_1_p6, dip_7404_2_p2, dip_7404_2_p4, dip_7404_2_p6,
       dip_7404_2_p8, dip_7410_1_p7, dip_7410_2_p1, dip_7410_2_p8, dip_7410_2_p10, dip_7432_1_p3,
       dip_7432_1_p6, nano_1_p2, nano_1_p3, nano_1_p4;

  // NANO nano_1: pin names not known; wires that end beside it: 1'b0, nano_1_p2, nano_1_p3, nano_1_p4, 1'b1, 1'b0, out_1
  // DIP_7404 dip_7404_1: pin names not known; wires that end beside it: nano_1_p2, dip_7404_1_p2, nano_1_p3, dip_7404_1_p4, nano_1_p4, dip_7404_1_p6, 1'b0, 1'b0, 1'b0
  // DIP_7410 dip_7410_1: pin names not known; wires that end beside it: nano_1_p2, dip_7404_1_p4, dip_7404_1_p2, nano_1_p3, dip_7404_1_p6, dip_7404_1_p6, dip_7410_1_p7, nano_1_p4, dip_7404_1_p2
  // DIP_7410 dip_7410_2: pin names not known; wires that end beside it: dip_7410_2_p1, nano_1_p4, nano_1_p3, 1'b0, 1'b0, 1'b0, dip_7404_1_p4, dip_7410_2_p8, nano_1_p2, dip_7410_2_p10, 1'b0, 1'b0, 1'b0
  // DIP_7404 dip_7404_2: pin names not known; wires that end beside it: dip_7410_1_p7, dip_7404_2_p2, dip_7410_2_p1, dip_7404_2_p4, dip_7410_2_p8, dip_7404_2_p6, dip_7410_2_p10, dip_7404_2_p8, 1'b0, 1'b0
  // DIP_7432 dip_7432_1: pin names not known; wires that end beside it: dip_7404_2_p2, dip_7404_2_p4, dip_7432_1_p3, dip_7432_1_p3, dip_7404_2_p6, dip_7432_1_p6, 1'b0, 1'b0, dip_7404_2_p8, dip_7432_1_p6, out_1

  // Notes on the sheet:
  //   3-Input Odd Parity with available ICs and NANO V3 Driver
endmodule

module main_xor (
);

  wire dip_7486_1_p3, dip_7486_1_p6, nano_1_p2, nano_1_p3, nano_1_p4;

  // NANO nano_1: pin names not known; wires that end beside it: 1'b0, nano_1_p2, nano_1_p3, nano_1_p4, 1'b1, 1'b0
  // DIP_7486 dip_7486_1: pin names not known; wires that end beside it: nano_1_p2, nano_1_p3, dip_7486_1_p3, dip_7486_1_p3, nano_1_p4, dip_7486_1_p6, 1'b0, 1'b0, 1'b0, 1'b0
  // Probe on dip_7486_1_p6

  // Notes on the sheet:
  //   3-Input Odd Parity with XOR and NANO V3 Driver
endmodule

module _3_Input_Odd_Parity (
  input  [2:0] in_1,
  output out_2
);

  wire and_1_out, and_2_out, and_3_out, and_4_out, not_1_out, not_2_out, not_3_out;

  not not_1 (not_1_out, in_1[2]);
  not not_2 (not_2_out, in_1[1]);
  not not_3 (not_3_out, in_1[0]);
  and and_1 (and_1_out, in_1[2], not_2_out, not_3_out);
  and and_2 (and_2_out, not_1_out, in_1[1], not_3_out);
  and and_3 (and_3_out, not_2_out, not_1_out, in_1[0]);
  and and_4 (and_4_out, in_1[0], in_1[1], in_1[2]);
  or or_1 (out_2, and_1_out, and_2_out, and_3_out, and_4_out);

  // Notes on the sheet:
  //   3-Input Odd Parity pure logic
endmodule

module _3_Input_Odd_Parity_Suboptimal (
  input  in_1,
  input  in_2,
  input  in_3,
  output out_4
);

  wire dip_7404_1_p2, dip_7404_1_p4, dip_7404_1_p6, dip_7404_2_p2, dip_7404_2_p4, dip_7404_2_p6,
       dip_7404_2_p8, dip_7410_1_p6, dip_7410_2_p2, dip_7410_2_p10, dip_7410_2_p12, dip_7432_1_p3,
       dip_7432_1_p6;

  // DIP_7404 dip_7404_1: pin names not known; wires that end beside it: in_1, dip_7404_1_p2, in_2, dip_7404_1_p4, in_3, dip_7404_1_p6, 1'b0, 1'b0, 1'b0
  // DIP_7410 dip_7410_1: pin names not known; wires that end beside it: in_1, dip_7404_1_p4, dip_7404_1_p2, in_2, dip_7404_1_p6, dip_7410_1_p6, in_3
  // DIP_7410 dip_7410_2: pin names not known; wires that end beside it: dip_7404_1_p6, dip_7410_2_p2, in_3, in_2, 1'b0, 1'b0, 1'b0, dip_7404_1_p2, dip_7404_1_p4, dip_7410_2_p10, in_1, dip_7410_2_p12, 1'b0, 1'b0, 1'b0
  // DIP_7404 dip_7404_2: pin names not known; wires that end beside it: dip_7410_1_p6, dip_7404_2_p2, dip_7410_2_p2, dip_7404_2_p4, dip_7410_2_p10, dip_7404_2_p6, dip_7410_2_p12, dip_7404_2_p8, 1'b0, 1'b0
  // DIP_7432 dip_7432_1: pin names not known; wires that end beside it: dip_7404_2_p2, dip_7404_2_p4, dip_7432_1_p3, dip_7432_1_p3, dip_7404_2_p6, dip_7432_1_p6, 1'b0, 1'b0, dip_7404_2_p8, dip_7432_1_p6, out_4

  // Notes on the sheet:
  //   3-Input Odd Parity with available ICs
endmodule

module _3_Input_Odd_Parity_Generated (
  input  a,
  input  b,
  input  c,
  output x
);

  wire and_1_out, and_2_out, and_3_out, and_4_out, not_1_out, not_2_out, not_3_out, not_4_out, not_5_out,
       not_6_out;

  not not_1 (not_1_out, a);
  not not_2 (not_2_out, b);
  not not_3 (not_3_out, a);
  not not_4 (not_4_out, c);
  not not_5 (not_5_out, b);
  not not_6 (not_6_out, c);
  and and_1 (and_1_out, not_1_out, not_2_out, c);
  and and_2 (and_2_out, not_3_out, b, not_4_out);
  and and_3 (and_3_out, a, not_5_out, not_6_out);
  and and_4 (and_4_out, a, b, c);
  or or_1 (x, and_1_out, and_2_out, and_3_out, and_4_out);
endmodule

module _3_Input_Odd_Parity_NAND_Only (
  input  a,
  input  b,
  input  c,
  output x
);

  wire nand_1_out, nand_2_out, nand_3_out, nand_4_out, nand_5_out, nand_6_out, nand_7_out, nand_8_out,
       nand_9_out, nand_10_out;

  nand nand_1 (nand_1_out, a, a);
  nand nand_2 (nand_2_out, b, b);
  nand nand_3 (nand_3_out, a, a);
  nand nand_4 (nand_4_out, c, c);
  nand nand_5 (nand_5_out, b, b);
  nand nand_6 (nand_6_out, c, c);
  nand nand_7 (nand_7_out, nand_1_out, nand_2_out, c);
  nand nand_8 (nand_8_out, nand_3_out, b, nand_4_out);
  nand nand_9 (nand_9_out, a, nand_5_out, nand_6_out);
  nand nand_10 (nand_10_out, a, b, c);
  nand nand_11 (x, nand_7_out, nand_8_out, nand_9_out, nand_10_out);
endmodule

module _3_input_Odd_Parity_XOR (
  input  IN3,
  input  IN2,
  input  IN1
);

  wire dip_7486_1_p3, dip_7486_1_p6;

  // DIP_7486 dip_7486_1: pin names not known; wires that end beside it: IN3, IN2, dip_7486_1_p3, dip_7486_1_p3, IN1, dip_7486_1_p6, 1'b0, 1'b0, 1'b0, 1'b0
  // Probe on dip_7486_1_p6
endmodule
